# Fritzing sketch Untitled Sketch (saved by Fritzing 0.9.3b)

parts:
  Part1 = Arduino Uno (Rev3) - ICSP
  GSM_SIM_GPSR_SMS_SIM900_SIM1 = SIM800L [package=THT]
  Part2 = Triple Axis Accelerometer Breakout - ADXL335
  Part3 = MQ-9 breakout
  J1 = Piezo Speaker

nets:
  N1: Part1.A0, Part3.AO
  N2: Part1.A1, Part2.XOUT
  N3: Part1.A2, Part2.YOUT
  N4: Part1.A3, Part2.ZOUT
  N5: Part1.D8, J1.pin2
  N6: Part1.D10_PWM/SS, GSM_SIM_GPSR_SMS_SIM900_SIM1.SIM_TXD
  N7: Part1.D11_PWM/MOSI, GSM_SIM_GPSR_SMS_SIM900_SIM1.SIM_RXD
  GND: Part1.GND, GSM_SIM_GPSR_SMS_SIM900_SIM1.GND, Part2.GND, Part3.GND, J1.pin1
  5V: Part1.5V, GSM_SIM_GPSR_SMS_SIM900_SIM1.5V, Part2.VCC, Part3.VCC

custom parts:
  MQ-9 breakout: SKU: 101284
